# Fritzing sketch Buttons (saved by Fritzing 1.0.8)
breadboards: 1

parts:
  S1 = Momentary Switch [package=ksa_sealed_tac_switch]
  S2 = Momentary Switch [package=ksa_sealed_tac_switch]
  R1 = Resistor [tolerance=±5% power=0.25W resistance=220 package=THT]
  R2 = Resistor [tolerance=±5% power=0.25W resistance=220 package=THT]
  Part1 = Arduino Uno (Rev3)
  LED1 = LED - 5mm [color="Blue (505nm)" current=0.030A package="5 mm [THT]"]  # not connected
  R3 = Resistor [tolerance=±5% power=0.25W resistance=220 package=THT]

nets:
  N1: S1.1, S2.1, Part1.5V
  N2: S1.3, R2.Pin_0
  N3: S1.4, Part1.D7
  N4: S2.3, R1.Pin_0
  N5: S2.4, Part1.D8
  N6: R1.Pin_1, R2.Pin_1, Part1.GND
  N7: Part1.D11_PWM/MOSI, R3.Pin_0
